# Fritzing sketch Moayad-Rafik (saved by Fritzing 0.9.2b)
breadboards: 1

parts:
  Part1 = Arduino Uno (Rev3)
  LED1 = LED - 5mm [color="Red (633nm)" package="5 mm [THT]"]
  R1 = Resistor [tolerance=±5% resistance=220 package=THT]
  D1 = Rectifier Diode [part_number=1N4001 package="300 mil [THT]"]
  LED2 = LED - 5mm [color="Red (633nm)" package="5 mm [THT]"]
  LED3 = LED - 5mm [color="Red (633nm)" package="5 mm [THT]"]
  LED4 = LED - 5mm [color="Red (633nm)" package="5 mm [THT]"]
  LED5 = LED - 5mm [color="Red (633nm)" package="5 mm [THT]"]
  R2 = Resistor [tolerance=±5% resistance=220 package=THT]
  R3 = Resistor [tolerance=±5% resistance=220 package=THT]
  R4 = Resistor [tolerance=±5% resistance=220 package=THT]
  Q1 = NPN-Transistor [package="TO92 [THT]"]

nets:
  N1: Part1.D8, LED3.anode
  N2: Part1.D9_PWM, LED4.anode
  N3: Part1.D10_PWM/SS, LED5.anode
  N4: Part1.D11_PWM/MOSI, LED2.anode
  N5: Part1.D2, R2.Pin_1
  N6: Part1.D3_PWM, R3.Pin_0
  N7: Part1.D4, R4.Pin_0
  N8: Part1.D5_PWM, R2.Pin_0, Q1.C
  N9: Part1.D6_PWM, R3.Pin_1, Q1.B
  N10: Part1.D7, R4.Pin_1, Q1.E
  N11: Part1.5V, D1.anode
  N12: Part1.GND, LED1.cathode, R1.Pin_0, LED2.cathode, LED3.cathode, LED4.cathode, LED5.cathode
  N13: LED1.anode, R1.Pin_1, D1.cathode
